# Fritzing sketch Sketch (saved by Fritzing 0.9.2b)
breadboards: 2

parts:
  Pro_Micro1 = Pro Micro
  ENCODER1 = Rotary Encoder with Knob
  LCM1602_IIC1 = LCM1602 IIC [part_number="LCM1602 IIC" chip_label="LCM1602 IIC" package="DIP (Dual Inline) [THT]"]
  LCD1_20x5 = LCD screen
  R2 = Resistor [tolerance=±5% resistance=10k package=THT]
  R3 = Resistor [tolerance=±5% resistance=10k package=THT]
  U2 = AUDIO-JACK2 [package=audio-jack]
  R7 = Resistor [tolerance=±5% resistance=10k package=THT]
  U5 = Optocoupler [package=THT]
  U6 = Optocoupler [package=THT]
  R8 = Resistor [tolerance=±5% resistance=1k package="1206 [SMD]"]
  R9 = Resistor [tolerance=±5% resistance=1k package="1206 [SMD]"]

nets:
  N1: Pro_Micro1.TX1, R3.Pin_0
  N2: Pro_Micro1.RX0, R2.Pin_0
  N3: Pro_Micro1.D2, LCM1602_IIC1.SDA
  N4: Pro_Micro1.D3, LCM1602_IIC1.SCL
  N5: Pro_Micro1.D4, ENCODER1.no_name_yet#4
  N6: Pro_Micro1.D16/MOSI, R9.Pin_0
  N7: Pro_Micro1.D14/MISO, R8.Pin_0
  N8: ENCODER1.no_name_yet#1, R2.Pin_1
  N9: ENCODER1.no_name_yet#2, ENCODER1.no_name_yet#5, LCM1602_IIC1.GND, U5.Pin_2, U6.Pin_2
  N10: ENCODER1.no_name_yet#3, R3.Pin_1
  VSS: LCM1602_IIC1.VSS, LCD1_20x5.VSS
  VDD: LCM1602_IIC1.VDD, LCD1_20x5.VDD
  N11: LCM1602_IIC1.V0, LCD1_20x5.V0
  N12: LCM1602_IIC1.RS, LCD1_20x5.RS
  N13: LCM1602_IIC1.RW, LCD1_20x5.R/W
  N14: LCM1602_IIC1.E, LCD1_20x5.E
  N15: LCM1602_IIC1.D0, LCD1_20x5.DB0
  N16: LCM1602_IIC1.D1, LCD1_20x5.DB1
  N17: LCM1602_IIC1.D2, LCD1_20x5.DB2
  N18: LCM1602_IIC1.D3, LCD1_20x5.DB3
  N19: LCM1602_IIC1.D4, LCD1_20x5.DB4
  N20: LCM1602_IIC1.D5, LCD1_20x5.DB5
  N21: LCM1602_IIC1.D6, LCD1_20x5.DB6
  N22: LCM1602_IIC1.D7, LCD1_20x5.DB7
  N23: LCM1602_IIC1.A, LCD1_20x5.LED-
  N24: LCM1602_IIC1.K, LCD1_20x5.LED+
  N25: LCM1602_IIC1.VCC, R7.Pin_0
  N26: LCM1602_IIC1.LED_A, LCM1602_IIC1.LED_B
  N27: U2.RING, U5.Pin_5
  N28: U2.SLEEVE, U5.Pin_4, U6.Pin_4
  N29: U2.TIP, U6.Pin_5
  N30: U5.Pin_1, R8.Pin_1
  N31: U6.Pin_1, R9.Pin_1

notes:
  Camera Remote Control
  Tip - Shutter
  Ring - Focus
  Sleeve - Camera Ground
  Turntable

custom parts:
  Pro Micro: The SparkFun Pro Micro is a complete USB-based microcontoller development system, in a very small footprint, capable of implementing many types of projects. All programming can be done via the USB port.
  Rotary Encoder with Knob: Rotary Encoder with 1/4" Shaft and Knob
  LCM1602 IIC: I2C-Module to use a 1602 or 2004 LCD on with the wire.h libory Serial LCD Modul
  LCD screen: A standard character display, usually with 2x16 characters. Comes in many colors.
